# Fritzing sketch circiut (saved by Fritzing 0.9.3b)
breadboards: 1

parts:
  Parça2 = Arduino Uno (Rev3)
  Power_plug1 = Power plug
  J5 = Power Jack [package=power_jack_smd]
  KY-1 = Keyes Relay [package=THT]
  S1 = Square Pushbutton
  U1 = LCD-16X2 [package=lcd-16x2_noholes]
  Keypad4x1 = Keypad Membran 4x4
  LCM1602_IIC1 = LCM1602 IIC [part_number="LCM1602 IIC" chip_label="LCM1602 IIC" package="DIP (Dual Inline) [THT]"]
  Buck_Convertor1 = Buck Convertor [part_number=LM2596 package=THT]
  SIM800L_BO1 = SIM800L BO
  Parça1 = RFID-RC522 [part_number=101218]
  C1 = Ceramic Capacitor [capacitance=100nF package="200 mil [THT, multilayer]"]

nets:
  N1: Parça2.A0, Keypad4x1.Pin5
  N2: Parça2.A1, Keypad4x1.Pin6
  N3: Parça2.A2, Keypad4x1.Pin7
  N4: Parça2.A3, Keypad4x1.Pin8
  N5: Parça2.A4/SDA, LCM1602_IIC1.SDA
  N6: Parça2.A5/SCL, LCM1602_IIC1.SCL
  N7: Parça2.D8, SIM800L_BO1.pin_4
  N8: Parça2.D9_PWM, Parça1.RST
  N9: Parça2.D10_PWM/SS, Parça1.SDA
  N10: Parça2.D11_PWM/MOSI, Parça1.MOSI
  N11: Parça2.D12/MISO, Parça1.MISO
  N12: Parça2.D13/SCK, Parça1.SCK
  GND: Parça2.GND, S1.leg0, LCM1602_IIC1.GND, Parça1.GND
  N13: Parça2.D0/RX, Keypad4x1.Pin4
  N14: Parça2.D2, Keypad4x1.Pin3
  N15: Parça2.D3_PWM, Keypad4x1.Pin2
  N16: Parça2.D4, Keypad4x1.Pin1
  N17: Parça2.D5_PWM, S1.leg1
  N18: Parça2.D6_PWM, KY-1.signal
  N19: Parça2.D7, SIM800L_BO1.pin_5
  3V3: Parça2.3V3, Parça1.3.3V
  5V: Parça2.5V, LCM1602_IIC1.VCC
  N20: Power_plug1.GND, KY-1.ground, KY-1.C, Buck_Convertor1.Negative_Input, C1.0
  N21: Power_plug1.VCC, J5.GNDBREAK, KY-1.power, Buck_Convertor1.Positive_Input
  VSS: U1.VSS, LCM1602_IIC1.VSS
  VDD: U1.VDD, LCM1602_IIC1.VDD
  N22: U1.VO, LCM1602_IIC1.V0
  N23: U1.RS, LCM1602_IIC1.RS
  N24: U1.R_W, LCM1602_IIC1.RW
  N25: U1.E, LCM1602_IIC1.E
  N26: U1.DB0, LCM1602_IIC1.D0
  N27: U1.DB1, LCM1602_IIC1.D1
  N28: U1.DB2, LCM1602_IIC1.D2
  N29: U1.DB3, LCM1602_IIC1.D3
  N30: U1.DB4, LCM1602_IIC1.D4
  N31: U1.DB5, LCM1602_IIC1.D5
  N32: U1.DB6, LCM1602_IIC1.D6
  N33: U1.DB7, LCM1602_IIC1.D7
  N34: U1.A, LCM1602_IIC1.A
  N35: U1.K, LCM1602_IIC1.K
  N36: Buck_Convertor1.Negative_Output, SIM800L_BO1.pin_6
  N37: Buck_Convertor1.Positive_Output, SIM800L_BO1.PIN2

notes:
  Nguồn 12VDC 3A
  Khóa điện 12V

custom parts:
  Keyes Relay: The Keyes 5V relay module is suitable for SCM development, home appliance control. It uses a 5V~12V TIL control signal which can control DC / AC signal.
  Keypad Membran 4x4: Membrane Keypad 4x4 Matrix
  LCM1602 IIC: I2C-Module to use a 1602 or 2004 LCD on with the wire.h libory Serial LCD Modul
  Buck Convertor: DC to DC buck convertor
